# Fritzing sketch dht22 (saved by Fritzing 0.9.10b)
breadboards: 1

parts:
  DHT1 = DHT22 Humidity and Temperature Sensor
  Mod1 = Raspberry Pi Pico

nets:
  N1: DHT1.VDD, Mod1.pin_36
  N2: DHT1.DATA, DHT1.GND, Mod1.pin_3, Mod1.pin_8, Mod1.pin_13, Mod1.pin_18, Mod1.pin_23, Mod1.pin_28, Mod1.pin_33, Mod1.pin_38

custom parts:
  Raspberry Pi Pico: Raspberry Pi Pico. Based around the RP2040 microcontroller the Pico is a low cost microcontroller device bringing Raspberry Pi quality, cost, and easy of use to the microcontroller space. Jan 2021, Split part in to two versions: tht (this one) and SMD. This one will drill holes for a .1 in header in pcb to allow plugging in the module as well as providing pads to solder the module to the top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

// code stored in the sketch: Untitled2.ino

