# Fritzing sketch oled13306 (saved by Fritzing 0.9.10b)
breadboards: 1

parts:
  Grove1 = Grove OLED 128x96
  Mod1 = Raspberry Pi Pico

nets:
  N1: Grove1.VCC, Mod1.pin_24
  N2: Mod1.pin_8, Mod1.pin_33, Mod1.pin_35, Mod1.pin_36, Mod1.pin_38

notes:
  接线管脚
  VCC-VCC 3V
  GND-GND
  GP13-PIN17 SCL
  GP12-PIN16 SDA

custom parts:
  Raspberry Pi Pico: Raspberry Pi Pico. Based around the RP2040 microcontroller the Pico is a low cost microcontroller device bringing Raspberry Pi quality, cost, and easy of use to the microcontroller space. Jan 2021, Split part in to two versions: tht (this one) and SMD. This one will drill holes for a .1 in header in pcb to allow plugging in the module as well as providing pads to solder the module to the top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
