# Fritzing sketch irq_button (saved by Fritzing 0.9.10b)
breadboards: 1

parts:
  S1 = Pushbutton [package="[THT]"]
  Mod1 = Raspberry Pi Pico
  R1 = Resistor [tolerance=±5% power=0.25 resistance=220 package=THT]
  LED1 = LED - 5mm [color="Red (633nm)" current=0.030 package="5 mm [THT]"]
  R2 = Resistor [tolerance=±5% power=0.25 resistance=1k package=THT]

nets:
  N1: S1.Pin_1, S1.Pin_2, Mod1.pin_20, LED1.anode
  N2: S1.Pin_3, S1.Pin_4, R2.Pin_1
  N3: Mod1.pin_6, Mod1.pin_35
  N4: Mod1.pin_12, Mod1.pin_27
  N5: Mod1.pin_13, Mod1.pin_23
  N6: R1.Pin_1, LED1.cathode

notes:
  按开关亮灯
  GP15-Pin20 电阻-led
  GP16-Pin20 开关

custom parts:
  Raspberry Pi Pico: Raspberry Pi Pico. Based around the RP2040 microcontroller the Pico is a low cost microcontroller device bringing Raspberry Pi quality, cost, and easy of use to the microcontroller space. Jan 2021, Split part in to two versions: tht (this one) and SMD. This one will drill holes for a .1 in header in pcb to allow plugging in the module as well as providing pads to solder the module to the top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
